// Logisim project Circuitos-M2.circ as structural Verilog: 7 circuits, main circuit main
module main (
  input  [7:0] in_1,
  input  in_2,
  output [15:0] out_3,
  output [15:0] out_4,
  output [7:0] out_5,
  output [15:0] out_6,
  output [15:0] out_7
);

  wire button_1_out, clock_1_out;

  Clock clock_1 (.out(clock_1_out));
  Button button_1 (.out(button_1_out));
  Register register_1 (.D(in_1), .en(in_2), .Q(out_5), .clk(clock_1_out), .clr(button_1_out));
endmodule

module Encoder_8_bits (
  output out_1,
  output out_2,
  output out_3,
  output out_4
);

  wire L_out, N_out, Ne_out, No_out, O_out, S_out, Se_out, So_out;

  Button No (.out(No_out));
  Button O (.out(O_out));
  Button So (.out(So_out));
  Button N (.out(N_out));
  Button Ne (.out(Ne_out));
  Button L (.out(L_out));
  Button Se (.out(Se_out));
  Button S (.out(S_out));
  or or_1 (out_2, No_out, O_out, So_out, S_out);
  or or_2 (out_3, No_out, O_out, Se_out, L_out);
  ExactlyOne xor_1 (
    .out(out_1), .in0(N_out), .in1(Ne_out), .in2(L_out), .in3(Se_out), .in4(S_out), .in5(So_out),
    .in6(O_out), .in7(No_out));
  or or_3 (out_4, No_out, So_out, Se_out, Ne_out);
endmodule

module Multiplexer (
  input  [15:0] in_1,
  input  [15:0] in_2,
  input  [15:0] in_3,
  input  [15:0] in_4,
  input  [15:0] in_5,
  input  [15:0] in_6,
  input  [15:0] in_7,
  input  [15:0] in_8,
  input  [2:0] in_9,
  output [18:0] out_10
);

  wire and_1_out, and_2_out, and_3_out, and_4_out, and_5_out, and_6_out, and_7_out, and_8_out, not_1_out,
       not_2_out, not_3_out, not_4_out, not_5_out, not_6_out, not_7_out, not_8_out, not_9_out, not_10_out,
       not_11_out, not_12_out;

  not not_1 (not_1_out, in_9[2]);
  assign out_10[15:0] = and_2_out ? in_1 : 16'bz;  // Controlled_Buffer controlled_buffer_1
  assign out_10[15:0] = and_1_out ? in_2 : 16'bz;  // Controlled_Buffer controlled_buffer_2
  and and_1 (and_1_out, not_4_out, not_6_out, in_9[0]);
  and and_2 (and_2_out, not_1_out, not_5_out, not_3_out);
  not not_2 (not_2_out, in_9[2]);
  not not_3 (not_3_out, in_9[0]);
  not not_4 (not_4_out, in_9[2]);
  not not_5 (not_5_out, in_9[1]);
  not not_6 (not_6_out, in_9[1]);
  assign out_10[15:0] = and_4_out ? in_3 : 16'bz;  // Controlled_Buffer controlled_buffer_3
  assign out_10[15:0] = and_3_out ? in_4 : 16'bz;  // Controlled_Buffer controlled_buffer_4
  and and_3 (and_3_out, not_7_out, in_9[1], in_9[0]);
  and and_4 (and_4_out, not_2_out, in_9[1], not_8_out);
  not not_7 (not_7_out, in_9[2]);
  not not_8 (not_8_out, in_9[0]);
  assign out_10[15:0] = and_6_out ? in_5 : 16'bz;  // Controlled_Buffer controlled_buffer_5
  assign out_10[15:0] = and_5_out ? in_6 : 16'bz;  // Controlled_Buffer controlled_buffer_6
  and and_5 (and_5_out, in_9[2], not_9_out, in_9[0]);
  and and_6 (and_6_out, in_9[2], not_11_out, not_10_out);
  not not_9 (not_9_out, in_9[1]);
  not not_10 (not_10_out, in_9[0]);
  not not_11 (not_11_out, in_9[1]);
  assign out_10[15:0] = and_7_out ? in_7 : 16'bz;  // Controlled_Buffer controlled_buffer_7
  assign out_10[15:0] = and_8_out ? in_8 : 16'bz;  // Controlled_Buffer controlled_buffer_8
  and and_7 (and_7_out, in_9[2], in_9[1], not_12_out);
  and and_8 (and_8_out, in_9[2], in_9[1], in_9[0]);
  not not_12 (not_12_out, in_9[0]);

  assign out_10[18:16] = in_9;
endmodule

module Demux (
  input  [15:0] in_1,
  input  [2:0] in_2,
  output [15:0] out_3,
  output [15:0] out_4,
  output [15:0] out_5,
  output [15:0] out_6,
  output [15:0] out_7,
  output [15:0] out_8,
  output [15:0] out_9,
  output [15:0] out_10
);

  wire and_1_out, and_2_out, and_3_out, and_4_out, and_5_out, and_6_out, and_7_out, and_8_out, not_1_out,
       not_2_out, not_3_out, not_4_out, not_5_out, not_6_out, not_7_out, not_8_out, not_9_out, not_10_out,
       not_11_out, not_12_out;

  assign out_3 = and_1_out ? in_1 : 16'bz;  // Controlled_Buffer controlled_buffer_1
  and and_1 (and_1_out, not_3_out, not_2_out, not_4_out);
  not not_1 (not_1_out, in_2[2]);
  not not_2 (not_2_out, in_2[1]);
  not not_3 (not_3_out, in_2[2]);
  not not_4 (not_4_out, in_2[0]);
  assign out_4 = and_2_out ? in_1 : 16'bz;  // Controlled_Buffer controlled_buffer_2
  assign out_5 = and_3_out ? in_1 : 16'bz;  // Controlled_Buffer controlled_buffer_3
  and and_2 (and_2_out, not_1_out, not_5_out, in_2[0]);
  and and_3 (and_3_out, not_8_out, in_2[1], not_6_out);
  not not_5 (not_5_out, in_2[1]);
  not not_6 (not_6_out, in_2[0]);
  not not_7 (not_7_out, in_2[2]);
  not not_8 (not_8_out, in_2[2]);
  assign out_6 = and_4_out ? in_1 : 16'bz;  // Controlled_Buffer controlled_buffer_4
  assign out_7 = and_5_out ? in_1 : 16'bz;  // Controlled_Buffer controlled_buffer_5
  and and_4 (and_4_out, not_7_out, in_2[1], in_2[0]);
  and and_5 (and_5_out, in_2[2], not_9_out, not_10_out);
  not not_9 (not_9_out, in_2[1]);
  not not_10 (not_10_out, in_2[0]);
  assign out_8 = and_6_out ? in_1 : 16'bz;  // Controlled_Buffer controlled_buffer_6
  assign out_9 = and_7_out ? in_1 : 16'bz;  // Controlled_Buffer controlled_buffer_7
  and and_6 (and_6_out, in_2[2], not_12_out, in_2[0]);
  and and_7 (and_7_out, in_2[2], in_2[1], not_11_out);
  not not_11 (not_11_out, in_2[0]);
  not not_12 (not_12_out, in_2[1]);
  assign out_10 = and_8_out ? in_1 : 16'bz;  // Controlled_Buffer controlled_buffer_8
  and and_8 (and_8_out, in_2[2], in_2[1], in_2[0]);
endmodule

module multiplexer_do_logsim (
  input  [15:0] in_1,
  input  [15:0] in_2,
  input  [15:0] in_3,
  input  [15:0] in_4,
  input  [15:0] in_5,
  input  [15:0] in_6,
  input  [15:0] in_7,
  input  [15:0] in_8,
  input  in_9,
  output [15:0] out_10,
  output [15:0] out_11,
  output [15:0] out_12,
  output [15:0] out_13,
  output [15:0] out_14,
  output [15:0] out_15,
  output [15:0] out_16,
  output [15:0] out_17
);

  wire clock_1_out, clock_2_out, comparator_1_eq, counter_1_carry, demultiplexer_1_out0,
       demultiplexer_1_out1, demultiplexer_1_out2, demultiplexer_1_out3, demultiplexer_1_out4,
       demultiplexer_1_out5, demultiplexer_1_out6, demultiplexer_1_out7, or_1_out, RESET_out;
  wire [2:0] counter_1_q;
  wire [7:0] counter_2_q;
  wire [15:0] demux_1_out_3, demux_1_out_4, demux_1_out_5, demux_1_out_6, demux_1_out_7, demux_1_out_8,
       demux_1_out_9, demux_1_out_10;
  wire [18:0] multiplexer_1_out_10;

  Clock clock_1 (.out(clock_1_out));
  Button RESET (.out(RESET_out));
  Multiplexer multiplexer_1 (
    .in_1(in_1), .in_2(in_2), .in_3(in_3), .in_4(in_4), .in_5(in_5), .in_6(in_6), .in_7(in_7), .in_8(in_8),
    .in_9(counter_1_q), .out_10(multiplexer_1_out_10));
  Counter #(.width(3), .max('h7)) counter_1 (
    .Q(counter_1_q), .carry(counter_1_carry), .clk(clock_1_out), .clr(or_1_out));  // open: load, D, count
  Counter #(.max('h7), .ongoal("stay")) counter_2 (
    .Q(counter_2_q), .clk(counter_1_carry), .clr(RESET_out));  // open: load, D, count, carry
  or or_1 (or_1_out, comparator_1_eq, RESET_out);
  Comparator comparator_1 (.a(counter_2_q), .b(8'h7), .eq(comparator_1_eq));  // open: gt, lt
  Demux demux_1 (
    .in_1(multiplexer_1_out_10[15:0]), .in_2(multiplexer_1_out_10[18:16]), .out_3(demux_1_out_3),
    .out_4(demux_1_out_4), .out_5(demux_1_out_5), .out_6(demux_1_out_6), .out_7(demux_1_out_7),
    .out_8(demux_1_out_8), .out_9(demux_1_out_9), .out_10(demux_1_out_10));
  Clock clock_2 (.out(clock_2_out));
  Demultiplexer #(.select(3)) demultiplexer_1 (
    .out0(demultiplexer_1_out0), .out1(demultiplexer_1_out1), .out2(demultiplexer_1_out2),
    .out3(demultiplexer_1_out3), .out4(demultiplexer_1_out4), .out5(demultiplexer_1_out5),
    .out6(demultiplexer_1_out6), .out7(demultiplexer_1_out7), .in(clock_2_out),
    .sel(multiplexer_1_out_10[18:16]));  // open: en
  Register #(.width(16)) register_1 (
    .D(demux_1_out_3), .en(in_9), .Q(out_10), .clk(demultiplexer_1_out0), .clr(RESET_out));
  Register #(.width(16)) register_2 (
    .D(demux_1_out_4), .en(in_9), .Q(out_11), .clk(demultiplexer_1_out1), .clr(RESET_out));
  Register #(.width(16)) register_3 (
    .D(demux_1_out_5), .en(in_9), .Q(out_12), .clk(demultiplexer_1_out2), .clr(RESET_out));
  Register #(.width(16)) register_4 (
    .D(demux_1_out_6), .en(in_9), .Q(out_13), .clk(demultiplexer_1_out3), .clr(RESET_out));
  Register #(.width(16)) register_5 (
    .D(demux_1_out_7), .en(in_9), .Q(out_14), .clk(demultiplexer_1_out4), .clr(RESET_out));
  Register #(.width(16)) register_6 (
    .D(demux_1_out_8), .en(in_9), .Q(out_15), .clk(demultiplexer_1_out5), .clr(RESET_out));
  Register #(.width(16)) register_7 (
    .D(demux_1_out_9), .en(in_9), .Q(out_16), .clk(demultiplexer_1_out6), .clr(RESET_out));
  Register #(.width(16)) register_8 (
    .D(demux_1_out_10), .en(in_9), .Q(out_17), .clk(demultiplexer_1_out7), .clr(RESET_out));
endmodule

module Snake_Game (
  output [3:0] out_1,
  output [3:0] out_2,
  output [1:0] out_3,
  output [1:0] out_4
);

  wire and_1_out, not_1_out;

  Joystick #(.bits(2)) joystick_1 (.x(out_3), .y(out_4));
  not not_1 (not_1_out, out_4[1]);
  and and_1 (and_1_out, out_4[0], out_4[1]);
  // AND_Gate and_2 has open pins: in0=out_4[0], in1=not_1_out, out=open
  Counter counter_1 ();  // open: load, D, count, Q, carry, clk, clr
endmodule

module Inversor (
  input  [15:0] in_1,
  output [15:0] out_2
);

  not not_1 (out_2[0], in_1[0]);
  not not_2 (out_2[1], in_1[1]);
  not not_3 (out_2[2], in_1[2]);
  not not_4 (out_2[3], in_1[3]);
  not not_5 (out_2[4], in_1[4]);
  not not_6 (out_2[5], in_1[5]);
  not not_7 (out_2[6], in_1[6]);
  not not_8 (out_2[7], in_1[7]);
  not not_9 (out_2[8], in_1[8]);
  not not_10 (out_2[9], in_1[9]);
  not not_11 (out_2[10], in_1[10]);
  not not_12 (out_2[11], in_1[11]);
  not not_13 (out_2[12], in_1[12]);
  not not_14 (out_2[13], in_1[13]);
  not not_15 (out_2[14], in_1[14]);
  not not_16 (out_2[15], in_1[15]);
endmodule
