// Logisim project Circuitos-M3.circ as structural Verilog: 5 circuits, main circuit main
module main (
  input  _0_Write___1___Load,
  input  Clear,
  output [7:0] out_3
);

  wire clock_1_out, controlled_buffer_1_out, counter_1_carry, not_1_out, not_2_out;
  wire [3:0] counter_1_q;
  wire [7:0] controlled_buffer_2_out, random_1_out;

  Random random_1 (.clk(controlled_buffer_1_out), .out(random_1_out));  // open: next, clr
  Counter #(.width(4), .max('hf)) counter_1 (
    .Q(counter_1_q), .carry(counter_1_carry), .clk(controlled_buffer_1_out));  // open: load, D, count, clr
  not not_1 (not_1_out, counter_1_carry);
  Clock clock_1 (.out(clock_1_out));
  assign controlled_buffer_1_out = not_1_out ? clock_1_out : 1'bz;  // Controlled_Buffer controlled_buffer_1
  assign controlled_buffer_2_out = not_2_out ? random_1_out : 8'bz;  // Controlled_Buffer controlled_buffer_2
  RAM #(.addrWidth(4)) ram_1 (
    .addr(counter_1_q), .data(controlled_buffer_2_out), .clk(controlled_buffer_1_out),
    .ld(_0_Write___1___Load), .clr(Clear));  // open: sel
  not not_2 (not_2_out, _0_Write___1___Load);
  assign out_3 = _0_Write___1___Load ? controlled_buffer_2_out : 8'bz;  // Controlled_Buffer controlled_buffer_3
endmodule

module \Laço_Dependente  (
);

  wire and_1_out, button_1_out, clock_1_out, comparator_1_lt, comparator_2_eq, or_1_out;
  wire [3:0] counter_1_q, counter_2_q;

  Counter #(.width(4), .max('h9)) counter_1 (
    .Q(counter_1_q), .clk(clock_1_out), .clr(and_1_out));  // open: load, D, count, carry
  Clock clock_1 (.out(clock_1_out));
  Button button_1 (.out(button_1_out));
  Comparator #(.width(4), .mode("unsigned")) comparator_1 (
    .a(counter_2_q), .b(counter_1_q), .lt(comparator_1_lt));  // open: gt, eq
  Counter #(.width(4), .max('h9)) counter_2 (
    .Q(counter_2_q), .clk(and_1_out), .clr(or_1_out));  // open: load, D, count, carry
  or or_1 (or_1_out, button_1_out, comparator_2_eq);
  and and_1 (and_1_out, comparator_1_lt, clock_1_out);
  Comparator #(.width(4)) comparator_2 (.a(counter_2_q), .b(4'b0111), .eq(comparator_2_eq));  // open: gt, lt
endmodule

module \Memória  (
  input  in_1,
  input  Enable,
  input  in_3,
  output [3:0] out_4,
  output [5:0] out_5
);

  wire and_1_out, clock_1_out, clock_2_out, comparator_1_gt, controlled_buffer_1_out, counter_3_carry,
       counter_4_carry, counter_5_carry, not_1_out, not_2_out;
  wire [3:0] ram_1_data, ram_2_data;
  wire [5:0] random_1_out;
  wire [9:0] counter_1_q;

  Clock clock_1 (.out(clock_1_out));
  Random #(.width(6), .seed(27)) random_1 (.clk(clock_1_out), .out(random_1_out));  // open: next, clr
  Clock clock_2 (.out(clock_2_out));
  Comparator #(.width(6), .mode("unsigned")) comparator_1 (
    .a(6'b101000), .b(random_1_out), .gt(comparator_1_gt));  // open: eq, lt
  Counter #(.width(10), .max('h27), .ongoal("stay")) counter_1 (.Q(counter_1_q));  // open: load, D, count, carry, clk, clr
  Counter #(.width(6), .max('h27), .ongoal("stay")) counter_2 (
    .Q(out_5), .clk(controlled_buffer_1_out), .clr(in_3));  // open: load, D, count, carry
  assign controlled_buffer_1_out = and_1_out ? clock_2_out : 1'bz;  // Controlled_Buffer controlled_buffer_1
  and and_1 (and_1_out, Enable, not_1_out);
  not not_1 (not_1_out, counter_3_carry);
  RAM #(.addrWidth(6), .dataWidth(4)) ram_1 (.addr(random_1_out), .data(ram_1_data), .ld(in_1));  // open: sel, clk, clr
  assign out_4 = comparator_1_gt ? ram_1_data : 4'bz;  // Controlled_Buffer controlled_buffer_2
  RAM #(.addrWidth(6), .dataWidth(4)) ram_2 (
    .addr(out_5), .data(ram_2_data), .clk(controlled_buffer_1_out), .ld(counter_3_carry), .clr(in_3));  // open: sel
  Counter #(.width(4), .max('ha)) counter_3 (
    .Q(ram_2_data), .carry(counter_3_carry), .clk(counter_5_carry), .clr(in_3));  // open: load, D, count
  Counter #(.width(1), .max('h1), .ongoal("stay")) counter_4 (
    .carry(counter_4_carry), .clk(controlled_buffer_1_out), .clr(in_3));  // open: load, D, count, Q
  Counter #(.width(4), .max('h3)) counter_5 (
    .carry(counter_5_carry), .clk(controlled_buffer_1_out), .clr(not_2_out));  // open: load, D, count, Q
  Register register_1 ();  // open: D, en, Q, clk, clr
  Register register_2 ();  // open: D, en, Q, clk, clr
  Register register_3 ();  // open: D, en, Q, clk, clr
  Register register_4 ();  // open: D, en, Q, clk, clr
  Register register_5 ();  // open: D, en, Q, clk, clr
  not not_2 (not_2_out, counter_4_carry);
  Register register_6 ();  // open: D, en, Q, clk, clr
  Register register_7 ();  // open: D, en, Q, clk, clr
endmodule

module Truco (
);

  \Memória  \memória_1  ();  // open: in_1, Enable, in_3, out_4, out_5
endmodule

module Selecionador (
);

  Register register_1 ();  // open: D, en, Q, clk, clr
  Register register_2 ();  // open: D, en, Q, clk, clr
  Register register_3 ();  // open: D, en, Q, clk, clr
  Register register_4 ();  // open: D, en, Q, clk, clr
  Register register_5 ();  // open: D, en, Q, clk, clr
  Register register_6 ();  // open: D, en, Q, clk, clr
  Register register_7 ();  // open: D, en, Q, clk, clr
endmodule
